# Fritzing sketch Fritzing (saved by Fritzing 0.9.3b)
breadboards: 1

parts:
  Part1 = Adafruit ESP32-S3 Reverse TFT Feather [part_number="Adafruit #5691"]
  Part2 = Adafruit VEML7700 STEMMA QT [part_number="Adafruit #5378"]
  Part3 = Adafruit BME680 [part_number="Adafruit #3660"]
  R1 = Resistor [tolerance=±1% resistance=22k package=THT]
  R2 = Resistor [tolerance=±1% resistance=12k package=THT]
  Part4 = Adafruit I2S Mic - SPH0645 [part_number="Adafruit #3421"]

nets:
  GND: Part1.GND, Part2.GND, Part3.GND, R2.Pin_0, Part4.GND
  VCC: Part1.VSENSOR, Part2.VCC, Part3.VCC
  N1: Part1.SDA, Part2.SDA, Part3.SDI/SDA
  N2: Part1.SCL, Part2.SCL, Part3.SCK/SCL
  3.3V: Part1.3.3V, Part4.VDD
  N3: Part1.VBUS, R1.Pin_1
  N4: Part1.D10, R1.Pin_0
  N5: Part1.D9, Part4.WS
  N6: Part1.D6, Part4.BCLK
  N7: Part1.D5, Part4.DATA

custom parts:
  Adafruit VEML7700 STEMMA QT: Vishay has a lot of light sensors out there, and this is a nice simple lux sensor that's easy to add to any microcontoller. Most light sensors just give you a number for brighter/darker ambient lighting. The VEML7700 makes your life easier by calculating the lux, which is an SI unit for light. You'll get more consistent readings between multiple sensors because you aren't dealing with some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
  Adafruit I2S Mic - SPH0645: For many microcontrollers, adding audio input is easy with one of our analog microphone breakouts. But as you get to bigger and better microcontrollers and microcomputers, you'll find that you don't always have an analog input, or maybe you want to avoid the noise that can seep in with an analog mic system. Once you get past 8-bit micros, you will often find an I2S peripheral, that can take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
